// Logisim project Tic-Tac-Toe_Modules.circ as structural Verilog: 15 circuits, main circuit DisplayControl
module DisplayControl (
  input  [3:0] \input ,
  output [17:0] outSignals_1_2,
  output [26:0] outSignals_3_4_5
);

  Multiplexer #(.width(18), .disabled(0)) multiplexer_1 (
    .in0(18'h1047c), .in1(18'h10501), .out(outSignals_1_2), .sel(\input [0]), .en(\input [1]));
  Pull_Resistor pull_resistor_1 (.node(outSignals_1_2));
  Multiplexer #(.width(27), .disabled(0)) multiplexer_2 (
    .in0(27'h4060301), .in1(27'h405044), .out(outSignals_3_4_5), .sel(\input [0]), .en(\input [1]));
  Pull_Resistor pull_resistor_2 (.node(outSignals_3_4_5));
endmodule

module DisplayReg1 (
  input  I_Osel,
  input  [3:0] I_Oadr,
  input  in_out,
  input  [3:0] I_Odat,
  output [3:0] out,
  output [3:0] value
);

  wire and_1_out, decoder_1_out0, decoder_1_out1;

  Register #(.width(4)) register_1 (.D(I_Odat), .Q(value), .clk(decoder_1_out0));  // open: en, clr
  assign out = decoder_1_out1 ? value : 4'bz;  // Controlled_Buffer controlled_buffer_1
  and and_1 (and_1_out, ~I_Oadr[3], ~I_Oadr[2], ~I_Oadr[1], I_Oadr[0], I_Osel);  // AND_Gate
  Decoder #(.disabled(0)) decoder_1 (.out0(decoder_1_out0), .out1(decoder_1_out1), .sel(in_out), .en(and_1_out));

  // Notes on the sheet:
  //   i/O Selecter
endmodule

module DisplayReg2 (
  input  I_Osel,
  input  [3:0] I_Oadr,
  input  in_out,
  input  [3:0] I_Odat,
  output [3:0] out,
  output [3:0] value
);

  wire and_1_out, decoder_1_out0, decoder_1_out1;

  Register #(.width(4)) register_1 (.D(I_Odat), .Q(value), .clk(decoder_1_out0));  // open: en, clr
  assign out = decoder_1_out1 ? value : 4'bz;  // Controlled_Buffer controlled_buffer_1
  and and_1 (and_1_out, ~I_Oadr[3], ~I_Oadr[2], I_Oadr[1], ~I_Oadr[0], I_Osel);  // AND_Gate
  Decoder #(.disabled(0)) decoder_1 (.out0(decoder_1_out0), .out1(decoder_1_out1), .sel(in_out), .en(and_1_out));

  // Notes on the sheet:
  //   i/O Selecter
endmodule

module DisplayReg3 (
  input  I_Osel,
  input  [3:0] I_Oadr,
  input  in_out,
  input  [3:0] I_Odat,
  output [3:0] out,
  output [3:0] value
);

  wire and_1_out, decoder_1_out0, decoder_1_out1;

  Register #(.width(4)) register_1 (.D(I_Odat), .Q(value), .clk(decoder_1_out0));  // open: en, clr
  assign out = decoder_1_out1 ? value : 4'bz;  // Controlled_Buffer controlled_buffer_1
  and and_1 (and_1_out, ~I_Oadr[3], ~I_Oadr[2], I_Oadr[1], I_Oadr[0], I_Osel);  // AND_Gate
  Decoder #(.disabled(0)) decoder_1 (.out0(decoder_1_out0), .out1(decoder_1_out1), .sel(in_out), .en(and_1_out));

  // Notes on the sheet:
  //   i/O Selecter
endmodule

module DisplayReg4 (
  input  I_Osel,
  input  [3:0] I_Oadr,
  input  in_out,
  input  [3:0] I_Odat,
  output [3:0] out,
  output [3:0] value
);

  wire and_1_out, decoder_1_out0, decoder_1_out1;

  Register #(.width(4)) register_1 (.D(I_Odat), .Q(value), .clk(decoder_1_out0));  // open: en, clr
  assign out = decoder_1_out1 ? value : 4'bz;  // Controlled_Buffer controlled_buffer_1
  and and_1 (and_1_out, ~I_Oadr[3], I_Oadr[2], ~I_Oadr[1], ~I_Oadr[0], I_Osel);  // AND_Gate
  Decoder #(.disabled(0)) decoder_1 (.out0(decoder_1_out0), .out1(decoder_1_out1), .sel(in_out), .en(and_1_out));

  // Notes on the sheet:
  //   i/O Selecter
endmodule

module DisplayReg5 (
  input  I_Osel,
  input  [3:0] I_Oadr,
  input  in_out,
  input  [3:0] I_Odat,
  output [3:0] out,
  output [3:0] value
);

  wire and_1_out, decoder_1_out0, decoder_1_out1;

  Register #(.width(4)) register_1 (.D(I_Odat), .Q(value), .clk(decoder_1_out0));  // open: en, clr
  assign out = decoder_1_out1 ? value : 4'bz;  // Controlled_Buffer controlled_buffer_1
  and and_1 (and_1_out, ~I_Oadr[3], I_Oadr[2], ~I_Oadr[1], I_Oadr[0], I_Osel);  // AND_Gate
  Decoder #(.disabled(0)) decoder_1 (.out0(decoder_1_out0), .out1(decoder_1_out1), .sel(in_out), .en(and_1_out));

  // Notes on the sheet:
  //   i/O Selecter
endmodule

module DisplayReg6 (
  input  I_Osel,
  input  [3:0] I_Oadr,
  input  in_out,
  input  [3:0] I_Odat,
  output [3:0] out,
  output [3:0] value
);

  wire and_1_out, decoder_1_out0, decoder_1_out1;

  Register #(.width(4)) register_1 (.D(I_Odat), .Q(value), .clk(decoder_1_out0));  // open: en, clr
  assign out = decoder_1_out1 ? value : 4'bz;  // Controlled_Buffer controlled_buffer_1
  and and_1 (and_1_out, ~I_Oadr[3], I_Oadr[2], I_Oadr[1], ~I_Oadr[0], I_Osel);  // AND_Gate
  Decoder #(.disabled(0)) decoder_1 (.out0(decoder_1_out0), .out1(decoder_1_out1), .sel(in_out), .en(and_1_out));

  // Notes on the sheet:
  //   i/O Selecter
endmodule

module DisplayReg7 (
  input  I_Osel,
  input  [3:0] I_Oadr,
  input  in_out,
  input  [3:0] I_Odat,
  output [3:0] out,
  output [3:0] value
);

  wire and_1_out, decoder_1_out0, decoder_1_out1;

  Register #(.width(4)) register_1 (.D(I_Odat), .Q(value), .clk(decoder_1_out0));  // open: en, clr
  assign out = decoder_1_out1 ? value : 4'bz;  // Controlled_Buffer controlled_buffer_1
  and and_1 (and_1_out, ~I_Oadr[3], I_Oadr[2], I_Oadr[1], I_Oadr[0], I_Osel);  // AND_Gate
  Decoder #(.disabled(0)) decoder_1 (.out0(decoder_1_out0), .out1(decoder_1_out1), .sel(in_out), .en(and_1_out));

  // Notes on the sheet:
  //   i/O Selecter
endmodule

module DisplayReg8 (
  input  I_Osel,
  input  [3:0] I_Oadr,
  input  in_out,
  input  [3:0] I_Odat,
  output [3:0] out,
  output [3:0] value
);

  wire and_1_out, decoder_1_out0, decoder_1_out1;

  Register #(.width(4)) register_1 (.D(I_Odat), .Q(value), .clk(decoder_1_out0));  // open: en, clr
  assign out = decoder_1_out1 ? value : 4'bz;  // Controlled_Buffer controlled_buffer_1
  and and_1 (and_1_out, I_Oadr[3], ~I_Oadr[2], ~I_Oadr[1], ~I_Oadr[0], I_Osel);  // AND_Gate
  Decoder #(.disabled(0)) decoder_1 (.out0(decoder_1_out0), .out1(decoder_1_out1), .sel(in_out), .en(and_1_out));

  // Notes on the sheet:
  //   i/O Selecter
endmodule

module DisplayReg9 (
  input  I_Osel,
  input  [3:0] I_Oadr,
  input  in_out,
  input  [3:0] I_Odat,
  output [3:0] out,
  output [3:0] value
);

  wire and_1_out, decoder_1_out0, decoder_1_out1;

  Register #(.width(4)) register_1 (.D(I_Odat), .Q(value), .clk(decoder_1_out0));  // open: en, clr
  assign out = decoder_1_out1 ? value : 4'bz;  // Controlled_Buffer controlled_buffer_1
  and and_1 (and_1_out, I_Oadr[3], ~I_Oadr[2], ~I_Oadr[1], I_Oadr[0], I_Osel);  // AND_Gate
  Decoder #(.disabled(0)) decoder_1 (.out0(decoder_1_out0), .out1(decoder_1_out1), .sel(in_out), .en(and_1_out));

  // Notes on the sheet:
  //   i/O Selecter
endmodule

module Win_loose_screen (
  input  I_O_sel,
  input  [3:0] I_O_Adr,
  input  in_out,
  input  [7:0] I_Odat,
  output player,
  output Draw,
  output computer,
  output [7:0] I_Odat_2
);

  wire and_4_out, decoder_1_out0, decoder_1_out1;
  wire [7:0] register_1_q;

  and and_1 (player, register_1_q[0], register_1_q[1]);
  and and_2 (Draw, register_1_q[0], ~register_1_q[1]);  // AND_Gate
  and and_3 (computer, ~register_1_q[0], register_1_q[1]);  // AND_Gate
  assign I_Odat_2 = decoder_1_out1 ? register_1_q : 8'bz;  // Controlled_Buffer controlled_buffer_1
  Decoder #(.disabled(0)) decoder_1 (.out0(decoder_1_out0), .out1(decoder_1_out1), .sel(in_out), .en(and_4_out));
  Register register_1 (.D(I_Odat), .Q(register_1_q), .clk(decoder_1_out0));  // open: en, clr
  and and_4 (and_4_out, I_O_Adr[3], I_O_Adr[2], ~I_O_Adr[1], ~I_O_Adr[0], I_O_sel);  // AND_Gate

  // Notes on the sheet:
  //   Page number
  //   i/O Selecter
endmodule

module Move_Selector (
  input  [3:0] S1,
  input  [3:0] S2,
  input  [3:0] S3,
  input  [3:0] S4,
  input  [3:0] S5,
  input  [3:0] S6,
  input  [3:0] S7,
  input  [3:0] S8,
  input  [3:0] S9,
  input  CL,
  output [7:0] Move
);

  wire and_3_out, and_4_out, and_5_out, and_6_out, and_7_out, and_8_out, and_11_out, and_12_out, and_13_out,
       and_14_out, and_15_out, and_16_out, and_17_out, and_18_out, and_19_out, and_20_out, and_21_out,
       and_22_out, and_23_out, and_24_out, and_25_out, and_30_out, and_31_out, and_32_out, and_33_out,
       and_34_out, and_35_out, and_38_out, and_39_out, and_40_out, and_41_out, and_42_out, and_43_out,
       and_46_out, and_47_out, and_48_out, and_49_out, and_50_out, and_51_out, and_52_out, and_53_out,
       and_54_out, and_55_out, and_56_out, and_57_out, and_58_out, and_59_out, and_60_out, and_63_out,
       and_64_out, and_65_out, and_66_out, and_67_out, and_68_out, and_71_out, and_72_out, and_73_out,
       and_74_out, and_77_out, and_78_out, and_79_out, and_80_out, and_81_out, and_82_out, and_83_out,
       and_84_out, and_85_out, and_86_out, and_87_out, and_88_out, and_89_out, and_90_out, and_91_out,
       and_92_out, and_93_out, and_94_out, and_95_out, and_96_out, and_97_out, and_98_out, and_99_out,
       and_100_out, and_101_out, and_102_out, and_103_out, and_104_out, and_105_out, and_106_out,
       and_107_out, and_108_out, and_109_out, and_110_out, and_111_out, and_112_out, and_113_out,
       and_114_out, and_115_out, and_116_out, and_117_out, and_118_out, and_119_out, and_120_out,
       and_121_out, and_122_out, and_123_out, and_124_out, and_125_out, and_126_out, and_127_out,
       and_128_out, and_129_out, and_130_out, not_10_out, or_1_out, or_2_out, or_3_out, or_4_out, or_5_out,
       or_6_out, or_7_out, or_8_out, or_9_out, or_10_out, or_11_out, or_12_out, or_13_out, S1_0, S1_X, S1_Z,
       S2_0, S2_X, S2_Z, S3_0, S3_X, S3_Z, S4_0, S4_X, S4_Z, S5_0, S5_X, S5_Z, S6_0, S6_X, S6_Z, S7_0, S7_X,
       S7_Z, S8_0, S8_X, S8_Z, S9_0, S9_X, S9_Z;
  wire [3:0] random_1_out;
  wire [7:0] Comb_0_1, Comb_0_2, Comb_0_3, Comb_0_4, Comb_0_5, Comb_0_6, Comb_0_7, Comb_0_8, Comb_0_OUT,
       Comb_X_1, Comb_X_2, Comb_X_3, Comb_X_4, Comb_X_5, Comb_X_6, Comb_X_7, Comb_X_8, Comb_X_OUT,
       controlled_buffer_66_out, Hardcoded_Move;

  and and_1 (S1_0, S1[1], ~S1[0]);  // AND_Gate
  and and_2 (S1_X, S1[1], S1[0]);
  not not_1 (S1_Z, S1[1]);
  and and_3 (and_3_out, S1_0, S2_0, S3_Z);
  assign Comb_0_1 = and_3_out ? 8'hf3 : 8'bz;  // Controlled_Buffer controlled_buffer_1
  and and_4 (and_4_out, S2_0, S5_0, S8_Z);
  assign Comb_0_4 = and_4_out ? 8'hf8 : 8'bz;  // Controlled_Buffer controlled_buffer_2
  and and_5 (and_5_out, S7_0, S8_0, S9_Z);
  assign Comb_0_7 = and_5_out ? 8'hf9 : 8'bz;  // Controlled_Buffer controlled_buffer_3
  and and_6 (and_6_out, S1_X, S2_X, S3_Z);
  assign Comb_X_1 = and_6_out ? 8'hf3 : 8'bz;  // Controlled_Buffer controlled_buffer_4
  and and_7 (and_7_out, S2_X, S5_X, S8_Z);
  assign Comb_X_4 = and_7_out ? 8'hf8 : 8'bz;  // Controlled_Buffer controlled_buffer_5
  and and_8 (and_8_out, S7_X, S8_X, S9_Z);
  assign Comb_X_7 = and_8_out ? 8'hf9 : 8'bz;  // Controlled_Buffer controlled_buffer_6
  and and_9 (S2_0, S2[1], ~S2[0]);  // AND_Gate
  and and_10 (S2_X, S2[1], S2[0]);
  not not_2 (S2_Z, S2[1]);
  and and_11 (and_11_out, S1_Z, S2_Z, S3_Z, S4_Z, S5_X, S6_Z, S7_Z, S8_Z, S9_Z);
  and and_12 (and_12_out, S1_Z, S2_Z, S3_Z, S4_X, S5_Z, S6_Z, S7_Z, S8_Z, S9_Z);
  and and_13 (and_13_out, S1_Z, S2_Z, S3_Z, S4_Z, S5_Z, S6_Z, S7_X, S8_Z, S9_Z);
  and and_14 (and_14_out, S1_X, S2_Z, S3_Z, S4_X, S5_0, S6_Z, S7_Z, S8_Z, S9_Z);
  and and_15 (and_15_out, S1_Z, S2_Z, S3_Z, S4_X, S5_0, S6_X, S7_Z, S8_Z, S9_Z);
  and and_16 (and_16_out, S1_Z, S2_Z, S3_X, S4_Z, S5_0, S6_Z, S7_Z, S8_Z, S9_X);
  and and_17 (and_17_out, S1_Z, S2_Z, S3_Z, S4_Z, S5_0, S6_X, S7_Z, S8_Z, S9_X);
  and and_18 (and_18_out, S1_0, S2_Z, S3_Z, S4_Z, S5_X, S6_Z, S7_Z, S8_X, S9_Z);
  and and_19 (and_19_out, S1_Z, S2_Z, S3_Z, S4_Z, S5_0, S6_X, S7_Z, S8_Z, S9_X);
  and and_20 (and_20_out, S1_0, S2_Z, S3_0);
  Pull_Resistor pull_resistor_1 (.node(Comb_0_1));
  and and_21 (and_21_out, S2_0, S5_Z, S8_0);
  Pull_Resistor pull_resistor_2 (.node(Comb_0_4));
  and and_22 (and_22_out, S7_0, S8_Z, S9_0);
  Pull_Resistor pull_resistor_3 (.node(Comb_0_7));
  and and_23 (and_23_out, S1_X, S2_Z, S3_X);
  Pull_Resistor pull_resistor_4 (.node(Comb_X_1));
  and and_24 (and_24_out, S2_X, S5_Z, S8_X);
  Pull_Resistor pull_resistor_5 (.node(Comb_X_4));
  and and_25 (and_25_out, S7_X, S8_Z, S9_X);
  Pull_Resistor pull_resistor_6 (.node(Comb_X_7));
  and and_26 (S3_0, S3[1], ~S3[0]);  // AND_Gate
  and and_27 (S3_X, S3[1], S3[0]);
  not not_3 (S3_Z, S3[1]);
  assign Hardcoded_Move = and_11_out ? 8'hf1 : 8'bz;  // Controlled_Buffer controlled_buffer_7
  assign Hardcoded_Move = and_12_out ? 8'hf5 : 8'bz;  // Controlled_Buffer controlled_buffer_8
  assign Hardcoded_Move = and_13_out ? 8'hf5 : 8'bz;  // Controlled_Buffer controlled_buffer_9
  assign Hardcoded_Move = and_14_out ? 8'hf7 : 8'bz;  // Controlled_Buffer controlled_buffer_10
  assign Hardcoded_Move = and_15_out ? 8'hf1 : 8'bz;  // Controlled_Buffer controlled_buffer_11
  assign Hardcoded_Move = and_16_out ? 8'hf6 : 8'bz;  // Controlled_Buffer controlled_buffer_12
  assign Hardcoded_Move = and_17_out ? 8'hf3 : 8'bz;  // Controlled_Buffer controlled_buffer_13
  assign Hardcoded_Move = and_18_out ? 8'hf2 : 8'bz;  // Controlled_Buffer controlled_buffer_14
  assign Hardcoded_Move = and_19_out ? 8'hf3 : 8'bz;  // Controlled_Buffer controlled_buffer_15
  assign Comb_0_1 = and_20_out ? 8'hf2 : 8'bz;  // Controlled_Buffer controlled_buffer_16
  assign Comb_0_4 = and_21_out ? 8'hf5 : 8'bz;  // Controlled_Buffer controlled_buffer_17
  assign Comb_0_7 = and_22_out ? 8'hf8 : 8'bz;  // Controlled_Buffer controlled_buffer_18
  assign Comb_X_1 = and_23_out ? 8'hf2 : 8'bz;  // Controlled_Buffer controlled_buffer_19
  assign Comb_X_4 = and_24_out ? 8'hf5 : 8'bz;  // Controlled_Buffer controlled_buffer_20
  assign Comb_X_7 = and_25_out ? 8'hf8 : 8'bz;  // Controlled_Buffer controlled_buffer_21
  and and_28 (S4_X, S4[1], S4[0]);
  and and_29 (S4_0, S4[1], ~S4[0]);  // AND_Gate
  not not_4 (S4_Z, S4[1]);
  and and_30 (and_30_out, S1_Z, S2_0, S3_0);
  assign Comb_0_1 = and_30_out ? 8'hf1 : 8'bz;  // Controlled_Buffer controlled_buffer_22
  and and_31 (and_31_out, S2_Z, S5_0, S8_0);
  assign Comb_0_4 = and_31_out ? 8'hf2 : 8'bz;  // Controlled_Buffer controlled_buffer_23
  and and_32 (and_32_out, S7_Z, S8_0, S9_0);
  assign Comb_0_7 = and_32_out ? 8'hf7 : 8'bz;  // Controlled_Buffer controlled_buffer_24
  and and_33 (and_33_out, S1_Z, S2_X, S3_X);
  assign Comb_X_1 = and_33_out ? 8'hf1 : 8'bz;  // Controlled_Buffer controlled_buffer_25
  and and_34 (and_34_out, S2_Z, S5_X, S8_X);
  assign Comb_X_4 = and_34_out ? 8'hf2 : 8'bz;  // Controlled_Buffer controlled_buffer_26
  and and_35 (and_35_out, S7_Z, S8_X, S9_X);
  assign Comb_X_7 = and_35_out ? 8'hf7 : 8'bz;  // Controlled_Buffer controlled_buffer_27
  and and_36 (S5_0, S5[1], ~S5[0]);  // AND_Gate
  and and_37 (S5_X, S5[1], S5[0]);
  not not_5 (S5_Z, S5[1]);
  and and_38 (and_38_out, S1_0, S4_0, S7_Z);
  assign Comb_0_2 = and_38_out ? 8'hf7 : 8'bz;  // Controlled_Buffer controlled_buffer_28
  Pull_Resistor pull_resistor_7 (.node(Comb_0_2));
  and and_39 (and_39_out, S4_0, S5_0, S6_Z);
  assign Comb_0_5 = and_39_out ? 8'hf6 : 8'bz;  // Controlled_Buffer controlled_buffer_29
  Pull_Resistor pull_resistor_8 (.node(Comb_0_5));
  and and_40 (and_40_out, S3_0, S5_0, S7_Z);
  assign Comb_0_8 = and_40_out ? 8'hf7 : 8'bz;  // Controlled_Buffer controlled_buffer_30
  Pull_Resistor pull_resistor_9 (.node(Comb_0_8));
  and and_41 (and_41_out, S1_X, S4_X, S7_Z);
  assign Comb_X_2 = and_41_out ? 8'hf7 : 8'bz;  // Controlled_Buffer controlled_buffer_31
  Pull_Resistor pull_resistor_10 (.node(Comb_X_2));
  and and_42 (and_42_out, S4_X, S5_X, S6_Z);
  assign Comb_X_5 = and_42_out ? 8'hf6 : 8'bz;  // Controlled_Buffer controlled_buffer_32
  Pull_Resistor pull_resistor_11 (.node(Comb_X_5));
  and and_43 (and_43_out, S3_X, S5_X, S7_Z);
  assign Comb_X_8 = and_43_out ? 8'hf7 : 8'bz;  // Controlled_Buffer controlled_buffer_33
  Pull_Resistor pull_resistor_12 (.node(Comb_X_8));
  and and_44 (S6_X, S6[1], S6[0]);
  and and_45 (S6_0, S6[1], ~S6[0]);  // AND_Gate
  not not_6 (S6_Z, S6[1]);
  and and_46 (and_46_out, S1_Z, S2_X, S3_Z, S4_Z, S5_Z, S6_Z, S7_Z, S8_Z, S9_Z);
  assign Hardcoded_Move = and_46_out ? 8'hf5 : 8'bz;  // Controlled_Buffer controlled_buffer_34
  assign Hardcoded_Move = and_47_out ? 8'hf5 : 8'bz;  // Controlled_Buffer controlled_buffer_35
  and and_47 (and_47_out, S1_Z, S2_Z, S3_Z, S4_Z, S5_Z, S6_X, S7_Z, S8_Z, S9_Z);
  and and_48 (and_48_out, S1_Z, S2_Z, S3_Z, S4_Z, S5_Z, S6_Z, S7_Z, S8_Z, S9_X);
  assign Hardcoded_Move = and_48_out ? 8'hf5 : 8'bz;  // Controlled_Buffer controlled_buffer_36
  assign Hardcoded_Move = and_49_out ? 8'hf1 : 8'bz;  // Controlled_Buffer controlled_buffer_37
  and and_49 (and_49_out, S1_Z, S2_X, S3_Z, S4_X, S5_0, S6_Z, S7_Z, S8_Z, S9_Z);
  and and_50 (and_50_out, S1_Z, S2_Z, S3_Z, S4_X, S5_0, S6_Z, S7_X, S8_Z, S9_Z);
  assign Hardcoded_Move = and_50_out ? 8'hf1 : 8'bz;  // Controlled_Buffer controlled_buffer_38
  assign Hardcoded_Move = and_51_out ? 8'hf9 : 8'bz;  // Controlled_Buffer controlled_buffer_39
  and and_51 (and_51_out, S1_Z, S2_Z, S3_Z, S4_Z, S5_0, S6_X, S7_X, S8_Z, S9_Z);
  and and_52 (and_52_out, S1_Z, S2_Z, S3_Z, S4_Z, S5_0, S6_Z, S7_X, S8_X, S9_Z);
  assign Hardcoded_Move = and_52_out ? 8'hf9 : 8'bz;  // Controlled_Buffer controlled_buffer_40
  assign Hardcoded_Move = and_53_out ? 8'hf3 : 8'bz;  // Controlled_Buffer controlled_buffer_41
  and and_53 (and_53_out, S1_0, S2_Z, S3_Z, S4_Z, S5_X, S6_Z, S7_Z, S8_Z, S9_X);
  and and_54 (and_54_out, S1_Z, S2_Z, S3_Z, S4_Z, S5_0, S6_Z, S7_X, S8_X, S9_Z);
  assign Hardcoded_Move = and_54_out ? 8'hf9 : 8'bz;  // Controlled_Buffer controlled_buffer_42
  and and_55 (and_55_out, S1_0, S4_Z, S7_0);
  assign Comb_0_2 = and_55_out ? 8'hf4 : 8'bz;  // Controlled_Buffer controlled_buffer_43
  and and_56 (and_56_out, S4_0, S5_Z, S6_0);
  assign Comb_0_5 = and_56_out ? 8'hf5 : 8'bz;  // Controlled_Buffer controlled_buffer_44
  and and_57 (and_57_out, S3_0, S5_Z, S7_0);
  assign Comb_0_8 = and_57_out ? 8'hf5 : 8'bz;  // Controlled_Buffer controlled_buffer_45
  and and_58 (and_58_out, S1_X, S4_Z, S7_X);
  assign Comb_X_2 = and_58_out ? 8'hf4 : 8'bz;  // Controlled_Buffer controlled_buffer_46
  and and_59 (and_59_out, S4_X, S5_Z, S6_X);
  assign Comb_X_5 = and_59_out ? 8'hf5 : 8'bz;  // Controlled_Buffer controlled_buffer_47
  and and_60 (and_60_out, S3_X, S5_Z, S7_X);
  assign Comb_X_8 = and_60_out ? 8'hf5 : 8'bz;  // Controlled_Buffer controlled_buffer_48
  and and_61 (S7_0, S7[1], ~S7[0]);  // AND_Gate
  and and_62 (S7_X, S7[1], S7[0]);
  not not_7 (S7_Z, S7[1]);
  and and_63 (and_63_out, S1_Z, S4_0, S7_0);
  assign Comb_0_2 = and_63_out ? 8'hf1 : 8'bz;  // Controlled_Buffer controlled_buffer_49
  and and_64 (and_64_out, S4_Z, S5_0, S6_0);
  assign Comb_0_5 = and_64_out ? 8'hf4 : 8'bz;  // Controlled_Buffer controlled_buffer_50
  and and_65 (and_65_out, S3_Z, S5_0, S7_0);
  assign Comb_0_8 = and_65_out ? 8'hf3 : 8'bz;  // Controlled_Buffer controlled_buffer_51
  and and_66 (and_66_out, S1_Z, S4_X, S7_X);
  assign Comb_X_2 = and_66_out ? 8'hf1 : 8'bz;  // Controlled_Buffer controlled_buffer_52
  and and_67 (and_67_out, S4_Z, S5_X, S6_X);
  assign Comb_X_5 = and_67_out ? 8'hf4 : 8'bz;  // Controlled_Buffer controlled_buffer_53
  and and_68 (and_68_out, S3_Z, S5_X, S7_X);
  assign Comb_X_8 = and_68_out ? 8'hf3 : 8'bz;  // Controlled_Buffer controlled_buffer_54
  and and_69 (S8_0, S8[1], ~S8[0]);  // AND_Gate
  and and_70 (S8_X, S8[1], S8[0]);
  not not_8 (S8_Z, S8[1]);
  and and_71 (and_71_out, S1_0, S5_0, S9_Z);
  assign Comb_0_3 = and_71_out ? 8'hf9 : 8'bz;  // Controlled_Buffer controlled_buffer_55
  and and_72 (and_72_out, S3_0, S6_0, S9_Z);
  assign Comb_0_6 = and_72_out ? 8'hf9 : 8'bz;  // Controlled_Buffer controlled_buffer_56
  and and_73 (and_73_out, S1_X, S5_X, S9_Z);
  assign Comb_X_3 = and_73_out ? 8'hf9 : 8'bz;  // Controlled_Buffer controlled_buffer_57
  and and_74 (and_74_out, S3_X, S6_X, S9_Z);
  assign Comb_X_6 = and_74_out ? 8'hf9 : 8'bz;  // Controlled_Buffer controlled_buffer_58
  and and_75 (S9_0, S9[1], ~S9[0]);  // AND_Gate
  and and_76 (S9_X, S9[1], S9[0]);
  not not_9 (S9_Z, S9[1]);
  and and_77 (and_77_out, S1_Z, S2_Z, S3_Z, S4_Z, S5_Z, S6_Z, S7_Z, S8_X, S9_Z);
  and and_78 (and_78_out, S1_X, S2_Z, S3_Z, S4_Z, S5_Z, S6_Z, S7_Z, S8_Z, S9_Z);
  and and_79 (and_79_out, S1_Z, S2_Z, S3_X, S4_Z, S5_Z, S6_Z, S7_Z, S8_Z, S9_Z);
  and and_80 (and_80_out, S1_Z, S2_Z, S3_X, S4_X, S5_0, S6_Z, S7_Z, S8_Z, S9_Z);
  and and_81 (and_81_out, S1_Z, S2_Z, S3_Z, S4_X, S5_0, S6_Z, S7_Z, S8_X, S9_Z);
  and and_82 (and_82_out, S1_Z, S2_Z, S3_Z, S4_Z, S5_0, S6_X, S7_Z, S8_X, S9_Z);
  and and_83 (and_83_out, S1_Z, S2_Z, S3_Z, S4_Z, S5_0, S6_Z, S7_X, S8_Z, S9_X);
  and and_84 (and_84_out, S1_Z, S2_Z, S3_Z, S4_Z, S5_0, S6_X, S7_Z, S8_X, S9_Z);
  and and_85 (and_85_out, S1_Z, S2_Z, S3_Z, S4_Z, S5_0, S6_Z, S7_X, S8_Z, S9_X);
  and and_86 (and_86_out, S1_0, S5_Z, S9_0);
  Pull_Resistor pull_resistor_13 (.node(Comb_0_3));
  and and_87 (and_87_out, S3_0, S6_Z, S9_0);
  Pull_Resistor pull_resistor_14 (.node(Comb_0_6));
  and and_88 (and_88_out, S1_X, S5_Z, S9_X);
  Pull_Resistor pull_resistor_15 (.node(Comb_X_3));
  and and_89 (and_89_out, S3_X, S6_Z, S9_X);
  Pull_Resistor pull_resistor_16 (.node(Comb_X_6));
  assign Hardcoded_Move = and_77_out ? 8'hf5 : 8'bz;  // Controlled_Buffer controlled_buffer_59
  assign Hardcoded_Move = and_78_out ? 8'hf5 : 8'bz;  // Controlled_Buffer controlled_buffer_60
  assign Hardcoded_Move = and_79_out ? 8'hf5 : 8'bz;  // Controlled_Buffer controlled_buffer_61
  assign Hardcoded_Move = and_80_out ? 8'hf1 : 8'bz;  // Controlled_Buffer controlled_buffer_62
  assign Hardcoded_Move = and_81_out ? 8'hf7 : 8'bz;  // Controlled_Buffer controlled_buffer_63
  assign Hardcoded_Move = and_82_out ? 8'hf9 : 8'bz;  // Controlled_Buffer controlled_buffer_64
  assign Hardcoded_Move = and_83_out ? 8'hf8 : 8'bz;  // Controlled_Buffer controlled_buffer_65
  assign controlled_buffer_66_out = and_84_out ? 8'hf9 : 8'bz;  // Controlled_Buffer controlled_buffer_66
  assign Hardcoded_Move = and_85_out ? 8'hf8 : 8'bz;  // Controlled_Buffer controlled_buffer_67
  assign Comb_0_3 = and_86_out ? 8'hf5 : 8'bz;  // Controlled_Buffer controlled_buffer_68
  assign Comb_0_6 = and_87_out ? 8'hf6 : 8'bz;  // Controlled_Buffer controlled_buffer_69
  assign Comb_X_3 = and_88_out ? 8'hf5 : 8'bz;  // Controlled_Buffer controlled_buffer_70
  assign Comb_X_6 = and_89_out ? 8'hf6 : 8'bz;  // Controlled_Buffer controlled_buffer_71
  Pull_Resistor pull_resistor_17 (.node(Hardcoded_Move));
  and and_90 (and_90_out, S1_Z, S5_0, S9_0);
  assign Comb_0_3 = and_90_out ? 8'hf1 : 8'bz;  // Controlled_Buffer controlled_buffer_72
  and and_91 (and_91_out, S3_Z, S6_0, S9_0);
  assign Comb_0_6 = and_91_out ? 8'hf3 : 8'bz;  // Controlled_Buffer controlled_buffer_73
  and and_92 (and_92_out, S1_Z, S5_X, S9_X);
  assign Comb_X_3 = and_92_out ? 8'hf1 : 8'bz;  // Controlled_Buffer controlled_buffer_74
  and and_93 (and_93_out, S3_Z, S6_X, S9_X);
  assign Comb_X_6 = and_93_out ? 8'hf3 : 8'bz;  // Controlled_Buffer controlled_buffer_75
  and and_94 (and_94_out, S1_Z, S2_Z, S3_Z, S4_X, S5_0, S6_Z, S7_Z, S8_Z, S9_X);
  assign Hardcoded_Move = and_94_out ? 8'hf7 : 8'bz;  // Controlled_Buffer controlled_buffer_76
  assign Hardcoded_Move = and_95_out ? 8'hf3 : 8'bz;  // Controlled_Buffer controlled_buffer_77
  and and_95 (and_95_out, S1_X, S2_Z, S3_Z, S4_Z, S5_0, S6_X, S7_Z, S8_Z, S9_Z);
  and and_96 (and_96_out, S1_X, S2_Z, S3_Z, S4_Z, S5_0, S6_Z, S7_Z, S8_Z, S9_X);
  assign Hardcoded_Move = and_96_out ? 8'hf4 : 8'bz;  // Controlled_Buffer controlled_buffer_78
  assign Hardcoded_Move = and_97_out ? 8'hf9 : 8'bz;  // Controlled_Buffer controlled_buffer_79
  and and_97 (and_97_out, S1_Z, S2_X, S3_Z, S4_Z, S5_0, S6_Z, S7_X, S8_Z, S9_Z);
  and and_98 (and_98_out, S1_Z, S2_Z, S3_X, S4_Z, S5_0, S6_X, S7_Z, S8_Z, S9_Z);
  assign Hardcoded_Move = and_98_out ? 8'hf9 : 8'bz;  // Controlled_Buffer controlled_buffer_80
  assign Hardcoded_Move = and_99_out ? 8'hf7 : 8'bz;  // Controlled_Buffer controlled_buffer_81
  and and_99 (and_99_out, S1_Z, S2_Z, S3_Z, S4_Z, S5_0, S6_Z, S7_Z, S8_X, S9_X);
  and and_100 (and_100_out, S1_0, S2_Z, S3_Z, S4_X, S5_X, S6_Z, S7_Z, S8_Z, S9_Z);
  assign Hardcoded_Move = and_100_out ? 8'hf6 : 8'bz;  // Controlled_Buffer controlled_buffer_82
  or or_1 (or_1_out, Comb_0_1[7], Comb_0_2[7]);
  and and_101 (and_101_out, ~Comb_0_1[7], Comb_0_2[7]);  // AND_Gate
  or or_2 (or_2_out, or_1_out, Comb_0_3[7]);
  assign Comb_0_OUT = Comb_0_1[7] ? Comb_0_1 : 8'bz;  // Controlled_Buffer controlled_buffer_83
  and and_102 (and_102_out, ~or_1_out, Comb_0_3[7]);  // AND_Gate
  or or_3 (or_3_out, or_2_out, Comb_0_4[7]);
  or or_4 (or_4_out, or_3_out, Comb_0_5[7]);
  assign Comb_0_OUT = and_101_out ? Comb_0_2 : 8'bz;  // Controlled_Buffer controlled_buffer_84
  assign Comb_0_OUT = and_102_out ? Comb_0_3 : 8'bz;  // Controlled_Buffer controlled_buffer_85
  and and_103 (and_103_out, ~or_2_out, Comb_0_4[7]);  // AND_Gate
  or or_5 (or_5_out, or_4_out, Comb_0_6[7]);
  or or_6 (or_6_out, or_5_out, Comb_0_7[7]);
  and and_104 (and_104_out, S1_X, S2_X, S3_Z, S4_Z, S5_0, S6_Z, S7_Z, S8_Z, S9_Z);
  assign Hardcoded_Move = and_104_out ? 8'hf3 : 8'bz;  // Controlled_Buffer controlled_buffer_86
  assign Hardcoded_Move = and_105_out ? 8'hf2 : 8'bz;  // Controlled_Buffer controlled_buffer_87
  and and_105 (and_105_out, S1_X, S2_Z, S3_Z, S4_Z, S5_0, S6_Z, S7_X, S8_Z, S9_Z);
  and and_106 (and_106_out, S1_Z, S2_X, S3_X, S4_Z, S5_0, S6_Z, S7_Z, S8_Z, S9_Z);
  assign Hardcoded_Move = and_106_out ? 8'hf1 : 8'bz;  // Controlled_Buffer controlled_buffer_88
  assign Hardcoded_Move = and_107_out ? 8'hf1 : 8'bz;  // Controlled_Buffer controlled_buffer_89
  and and_107 (and_107_out, S1_Z, S2_X, S3_Z, S4_Z, S5_0, S6_Z, S7_Z, S8_X, S9_Z);
  and and_108 (and_108_out, S1_Z, S2_Z, S3_X, S4_Z, S5_0, S6_Z, S7_X, S8_Z, S9_Z);
  assign Hardcoded_Move = and_108_out ? 8'hf4 : 8'bz;  // Controlled_Buffer controlled_buffer_90
  assign Hardcoded_Move = and_109_out ? 8'hf8 : 8'bz;  // Controlled_Buffer controlled_buffer_91
  and and_109 (and_109_out, S1_0, S2_X, S3_Z, S4_Z, S5_X, S6_Z, S7_Z, S8_Z, S9_Z);
  and and_110 (and_110_out, S1_0, S2_Z, S3_Z, S4_Z, S5_X, S6_X, S7_Z, S8_Z, S9_Z);
  assign Hardcoded_Move = and_110_out ? 8'hf4 : 8'bz;  // Controlled_Buffer controlled_buffer_92
  assign Comb_0_OUT = and_103_out ? Comb_0_4 : 8'bz;  // Controlled_Buffer controlled_buffer_93
  and and_111 (and_111_out, ~or_3_out, Comb_0_5[7]);  // AND_Gate
  and and_112 (and_112_out, ~or_4_out, Comb_0_6[7]);  // AND_Gate
  assign Comb_0_OUT = and_111_out ? Comb_0_5 : 8'bz;  // Controlled_Buffer controlled_buffer_94
  and and_113 (and_113_out, ~or_5_out, Comb_0_7[7]);  // AND_Gate
  assign Comb_0_OUT = and_112_out ? Comb_0_6 : 8'bz;  // Controlled_Buffer controlled_buffer_95
  assign Comb_0_OUT = and_113_out ? Comb_0_7 : 8'bz;  // Controlled_Buffer controlled_buffer_96
  and and_114 (and_114_out, ~or_6_out, Comb_0_8[7]);  // AND_Gate
  Random #(.width(4), .seed(123)) random_1 (.clk(CL), .out(random_1_out));  // open: next, clr
  and and_115 (and_115_out, S1_X, S2_Z, S3_X, S4_Z, S5_0, S6_Z, S7_Z, S8_Z, S9_Z);
  assign Hardcoded_Move = and_115_out ? 8'hf2 : 8'bz;  // Controlled_Buffer controlled_buffer_97
  assign Hardcoded_Move = and_116_out ? 8'hf7 : 8'bz;  // Controlled_Buffer controlled_buffer_98
  and and_116 (and_116_out, S1_X, S2_Z, S3_Z, S4_Z, S5_0, S6_Z, S7_Z, S8_X, S9_Z);
  and and_117 (and_117_out, S1_Z, S2_X, S3_Z, S4_Z, S5_0, S6_X, S7_Z, S8_Z, S9_Z);
  assign Hardcoded_Move = and_117_out ? 8'hf3 : 8'bz;  // Controlled_Buffer controlled_buffer_99
  assign Hardcoded_Move = and_118_out ? 8'hf3 : 8'bz;  // Controlled_Buffer controlled_buffer_100
  and and_118 (and_118_out, S1_Z, S2_X, S3_Z, S4_Z, S5_0, S6_Z, S7_Z, S8_Z, S9_X);
  and and_119 (and_119_out, S1_Z, S2_Z, S3_X, S4_Z, S5_0, S6_Z, S7_Z, S8_X, S9_Z);
  assign Hardcoded_Move = and_119_out ? 8'hf9 : 8'bz;  // Controlled_Buffer controlled_buffer_101
  assign Hardcoded_Move = and_120_out ? 8'hf7 : 8'bz;  // Controlled_Buffer controlled_buffer_102
  and and_120 (and_120_out, S1_0, S2_Z, S3_X, S4_Z, S5_X, S6_Z, S7_Z, S8_Z, S9_Z);
  and and_121 (and_121_out, S1_0, S2_Z, S3_Z, S4_Z, S5_X, S6_Z, S7_X, S8_Z, S9_Z);
  assign Hardcoded_Move = and_121_out ? 8'hf3 : 8'bz;  // Controlled_Buffer controlled_buffer_103
  assign Comb_0_OUT = and_114_out ? Comb_0_8 : 8'bz;  // Controlled_Buffer controlled_buffer_104
  Pull_Resistor pull_resistor_18 (.node(Comb_0_OUT));
  and and_122 (and_122_out, ~Comb_0_OUT[7], Comb_X_OUT[7]);  // AND_Gate
  assign Comb_X_OUT = and_125_out ? Comb_X_7 : 8'bz;  // Controlled_Buffer controlled_buffer_105
  assign Comb_X_OUT = and_124_out ? Comb_X_8 : 8'bz;  // Controlled_Buffer controlled_buffer_106
  Pull_Resistor pull_resistor_19 (.node(Comb_X_OUT));
  assign Move = Comb_0_OUT[7] ? Comb_0_OUT : 8'bz;  // Controlled_Buffer controlled_buffer_107
  assign Move = and_122_out ? Comb_X_OUT : 8'bz;  // Controlled_Buffer controlled_buffer_108
  and and_123 (and_123_out, ~and_122_out, Hardcoded_Move[7]);  // AND_Gate
  or or_7 (or_7_out, Comb_0_OUT[7], Comb_X_OUT[7], Hardcoded_Move[7]);
  not not_10 (not_10_out, or_7_out);
  assign Move = not_10_out ? {4'b1111, random_1_out} : 8'bz;  // Controlled_Buffer controlled_buffer_109
  assign Comb_X_OUT = and_127_out ? Comb_X_6 : 8'bz;  // Controlled_Buffer controlled_buffer_110
  and and_124 (and_124_out, ~or_9_out, Comb_X_8[7]);  // AND_Gate
  assign Move = and_123_out ? Hardcoded_Move : 8'bz;  // Controlled_Buffer controlled_buffer_111
  assign Comb_X_OUT = and_126_out ? Comb_X_5 : 8'bz;  // Controlled_Buffer controlled_buffer_112
  and and_125 (and_125_out, ~or_8_out, Comb_X_7[7]);  // AND_Gate
  assign Comb_X_OUT = and_128_out ? Comb_X_4 : 8'bz;  // Controlled_Buffer controlled_buffer_113
  and and_126 (and_126_out, ~or_11_out, Comb_X_5[7]);  // AND_Gate
  and and_127 (and_127_out, ~or_10_out, Comb_X_6[7]);  // AND_Gate
  or or_8 (or_8_out, or_10_out, Comb_X_6[7]);
  or or_9 (or_9_out, or_8_out, Comb_X_7[7]);
  assign Comb_X_OUT = and_129_out ? Comb_X_3 : 8'bz;  // Controlled_Buffer controlled_buffer_114
  and and_128 (and_128_out, ~or_12_out, Comb_X_4[7]);  // AND_Gate
  or or_10 (or_10_out, or_11_out, Comb_X_5[7]);
  assign Comb_X_OUT = Comb_X_1[7] ? Comb_X_1 : 8'bz;  // Controlled_Buffer controlled_buffer_115
  assign Comb_X_OUT = and_130_out ? Comb_X_2 : 8'bz;  // Controlled_Buffer controlled_buffer_116
  and and_129 (and_129_out, ~or_13_out, Comb_X_3[7]);  // AND_Gate
  or or_11 (or_11_out, or_12_out, Comb_X_4[7]);
  and and_130 (and_130_out, ~Comb_X_1[7], Comb_X_2[7]);  // AND_Gate
  or or_12 (or_12_out, or_13_out, Comb_X_3[7]);
  or or_13 (or_13_out, Comb_X_1[7], Comb_X_2[7]);

  // Notes on the sheet:
  //   00*
  //   ---
  //   ---
  //   -0-
  //   -0-
  //   -*-
  //   ---
  //   ---
  //   00*
  //   XX*
  //   ---
  //   ---
  //   -X-
  //   -X-
  //   -*-
  //   ---
  //   ---
  //   XX*
  //   *--
  //   -X-
  //   ---
  //   ---
  //   X*-
  //   ---
  //   ---
  //   -*-
  //   X--
  //   X--
  //   X0-
  //   *--
  //   *--
  //   X0X
  //   ---
  //   --X
  //   -0*
  //   --X
  //   --*
  //   -0X
  //   --X
  //   0*-
  //   -X-
  //   -X-
  //   --*
  //   -0X
  //   --X
  //   0*0
  //   ---
  //   ---
  //   -0-
  //   -*-
  //   -0-
  //   ---
  //   ---
  //   0*0
  //   X*X
  //   ---
  //   ---
  //   -X-
  //   -*-
  //   -X-
  //   ---
  //   ---
  //   X*X
  //   *00
  //   ---
  //   ---
  //   -*-
  //   -0-
  //   -0-
  //   ---
  //   ---
  //   *00
  //   *XX
  //   ---
  //   ---
  //   -*-
  //   -X-
  //   -X-
  //   ---
  //   ---
  //   *XX
  //   0--
  //   0--
  //   *--
  //   ---
  //   00*
  //   ---
  //   --0
  //   -0-
  //   *--
  //   X--
  //   X--
  //   *--
  //   ---
  //   XX*
  //   ---
  //   --X
  //   -X-
  //   *--
  //   -X-
  //   -*-
  //   ---
  //   ---
  //   -*X
  //   ---
  //   ---
  //   -*-
  //   --X
  //   *X-
  //   X0-
  //   ---
  //   *--
  //   X0-
  //   X--
  //   ---
  //   -0X
  //   X-*
  //   ---
  //   -0-
  //   XX*
  //   0-*
  //   -X-
  //   --X
  //   ---
  //   -0-
  //   XX*
  //   0--
  //   *--
  //   0--
  //   ---
  //   0*0
  //   ---
  //   --0
  //   -*-
  //   0--
  //   X--
  //   *--
  //   X--
  //   ---
  //   X*X
  //   ---
  //   --X
  //   -*-
  //   X--
  //   *--
  //   0--
  //   0--
  //   ---
  //   *00
  //   ---
  //   --*
  //   -0-
  //   0--
  //   *--
  //   X--
  //   X--
  //   ---
  //   *XX
  //   ---
  //   --*
  //   -X-
  //   X--
  //   0--
  //   -0-
  //   --*
  //   --0
  //   --0
  //   --*
  //   X--
  //   -X-
  //   --*
  //   --X
  //   --X
  //   --*
  //   ---
  //   -*-
  //   -X-
  //   X--
  //   -*-
  //   ---
  //   --X
  //   -*-
  //   ---
  //   *-X
  //   X0-
  //   ---
  //   ---
  //   X0-
  //   *X-
  //   ---
  //   -0X
  //   -X*
  //   ---
  //   -0-
  //   X*X
  //   ---
  //   -0X
  //   -X*
  //   ---
  //   -0-
  //   X*X
  //   0--
  //   -*-
  //   --0
  //   --0
  //   --*
  //   --0
  //   X--
  //   -*-
  //   --X
  //   --X
  //   --*
  //   --X
  //   *--
  //   -0-
  //   --0
  //   --*
  //   --0
  //   --0
  //   *--
  //   -X-
  //   --X
  //   --*
  //   --X
  //   --X
  //   ---
  //   X0-
  //   *-X
  //   X-*
  //   -0X
  //   ---
  //   X--
  //   *0-
  //   --X
  //   -X-
  //   -0-
  //   X-*
  //   --X
  //   -0X
  //   --*
  //   ---
  //   -0-
  //   *XX
  //   0--
  //   XX*
  //   ---
  //   Hardcoded first or second move
  //   XX*
  //   -0-
  //   ---
  //   X--
  //   *0-
  //   X--
  //   *XX
  //   -0-
  //   ---
  //   *X-
  //   -0-
  //   -X-
  //   --X
  //   *0-
  //   X--
  //   0X-
  //   -X-
  //   -*-
  //   0--
  //   *XX
  //   ---
  //   X*X
  //   -0-
  //   ---
  //   X--
  //   -0-
  //   *X-
  //   -X*
  //   -0X
  //   ---
  //   -X*
  //   -0-
  //   --X
  //   --X
  //   -0-
  //   -X*
  //   0-X
  //   -X-
  //   *--
  //   0-*
  //   -X-
  //   X--
endmodule

module Display_controller_up (
  input  [3:0] S3,
  input  [3:0] S7,
  input  [3:0] S2,
  input  [3:0] S4,
  input  [3:0] S6,
  input  [3:0] S8,
  input  [3:0] S1,
  input  [3:0] S5,
  input  [3:0] S9,
  output [11:0] Col0,
  output [11:0] Col0_plus,
  output [11:0] Col1,
  output [11:0] Col2,
  output [11:0] Col3,
  output [11:0] Col4,
  output [11:0] Col5,
  output [11:0] Col10_minus,
  output [11:0] Col6,
  output [11:0] Col7,
  output [11:0] Col8,
  output [11:0] Col9,
  output [11:0] Col10,
  output [11:0] Col10_plus,
  output [11:0] Col11,
  output [11:0] Col12,
  output [11:0] Col13,
  output [11:0] Col14,
  output [11:0] Col15,
  output [11:0] Col20_minus,
  output [11:0] Col16,
  output [11:0] Col17,
  output [11:0] Col18,
  output [11:0] Col19,
  output [11:0] Col20,
  output [11:0] Col20_plus,
  output [11:0] Col25,
  output [11:0] Col30_minus,
  output [11:0] Col30,
  output [11:0] Col26,
  output [11:0] Col27,
  output [11:0] Col28,
  output [11:0] Col29,
  output [11:0] Col21,
  output [11:0] Col22,
  output [11:0] Col23,
  output [11:0] Col24
);

  wire _0Set1, _0Set2, _0Set3, _0Set4, _0Set5, _0Set6, _0Set7, _0Set8, _0Set9, _456, _789, M1, M2, M3, M4,
       M5, M6, M7, M8, M9;
  wire [4:4] _11, _12, _13, _14, _21, _22, _23, _24, _31, _32, _33, _34, or_24_out, or_25_out, or_26_out;
  wire [8:0] _15, _25, _35, _41, _42, _43, _44, _45, _51, _52, _53, _54, _55, _61, _62, _63, _64, _65, _71,
       _72, _73, _74, _75, _81, _82, _83, _84, _85, _91, _92, _93, _94, _95;

  or or_1 (Col1[9], Col0_plus[10], Col9[9]);
  or or_2 (Col1[5], _11[4], Col0_plus[5]);
  or or_3 (Col11[5], _21[4], Col0_plus[5]);
  or or_4 (Col21[5], _31[4], Col0_plus[5]);
  or or_5 (Col21[1], Col29[1], Col20_plus[0]);
  DisplayControl displaycontrol_1 (
    .\input (S2),
    .outSignals_1_2({Col12[1], Col12[2], Col12[3], Col12[4], _22[4], Col12[6], Col12[7], Col12[8], Col12[9], Col11[1], Col11[2], Col11[3], Col11[4], _21[4], Col11[6], Col11[7], Col11[8], Col11[9]}),
    .outSignals_3_4_5({_25, Col14[1], Col14[2], Col14[3], Col14[4], _24[4], Col14[6], Col14[7], Col14[8], Col14[9], Col13[1], Col13[2], Col13[3], Col13[4], _23[4], Col13[6], Col13[7], Col13[8], Col13[9]}));
  DisplayControl displaycontrol_2 (
    .\input (S1),
    .outSignals_1_2({Col2[1], Col2[2], Col2[3], Col2[4], _12[4], Col2[6], Col2[7], Col8[8], Col2[9], Col1[1], Col1[2], Col1[3], Col1[4], _11[4], Col1[6], Col1[7], Col1[8], Col9[9]}),
    .outSignals_3_4_5({_15, Col4[1], Col4[2], Col4[3], Col4[4], _14[4], Col6[6], Col4[7], Col4[8], Col4[9], Col3[1], Col3[2], Col3[3], Col3[4], _13[4], Col3[6], Col7[7], Col3[8], Col3[9]}));
  DisplayControl displaycontrol_3 (
    .\input (S3),
    .outSignals_1_2({Col22[1], Col28[2], Col22[3], Col22[4], _32[4], Col22[6], Col22[7], Col22[8], Col22[9], Col29[1], Col21[2], Col21[3], Col21[4], _31[4], Col21[6], Col21[7], Col21[8], Col21[9]}),
    .outSignals_3_4_5({_35, Col24[1], Col24[2], Col24[3], Col26[4], _34[4], Col24[6], Col24[7], Col24[8], Col24[9], Col23[1], Col23[2], Col27[3], Col23[4], _33[4], Col23[6], Col23[7], Col23[8], Col23[9]}));
  DisplayControl displaycontrol_4 (.\input (S4), .outSignals_1_2({_42, _41}), .outSignals_3_4_5({_45, _44, _43}));
  DisplayControl displaycontrol_5 (.\input (S7), .outSignals_1_2({_72, _71}), .outSignals_3_4_5({_75, _74, _73}));
  DisplayControl displaycontrol_6 (.\input (S5), .outSignals_1_2({_52, _51}), .outSignals_3_4_5({_55, _54, _53}));
  DisplayControl displaycontrol_7 (.\input (S6), .outSignals_1_2({_62, _61}), .outSignals_3_4_5({_65, _64, _63}));
  or or_6 (Col2[8], Col0_plus[10], Col8[8]);
  or or_7 (Col2[5], _12[4], Col0_plus[5]);
  or or_8 (Col12[5], _22[4], Col0_plus[5]);
  or or_9 (Col22[5], _32[4], Col0_plus[5]);
  or or_10 (Col22[2], Col28[2], Col20_plus[0]);
  DisplayControl displaycontrol_8 (.\input (S8), .outSignals_1_2({_82, _81}), .outSignals_3_4_5({_85, _84, _83}));
  DisplayControl displaycontrol_9 (.\input (S9), .outSignals_1_2({_92, _91}), .outSignals_3_4_5({_95, _94, _93}));
  or or_11 (Col3[7], Col0_plus[10], Col7[7]);
  or or_12 (Col3[5], _13[4], Col0_plus[5]);
  or or_13 (Col13[5], _23[4], Col0_plus[5]);
  or or_14 (Col23[5], _33[4], Col0_plus[5]);
  or or_15 (Col23[3], Col27[3], Col20_plus[0]);
  and and_1 (_0Set2, S2[1], ~S2[0]);  // AND_Gate
  and and_2 (_0Set1, S1[1], ~S1[0]);  // AND_Gate
  and and_3 (Col0_plus[5], _0Set1, _0Set2, _0Set3);
  and and_4 (Col5[10], _0Set1, _0Set4, _0Set7);
  and and_5 (_0Set4, S4[1], ~S4[0]);  // AND_Gate
  and and_6 (_0Set3, S3[1], ~S3[0]);  // AND_Gate
  and and_7 (_0Set5, S5[1], ~S5[0]);  // AND_Gate
  and and_8 (_456, _0Set4, _0Set5, _0Set6);
  and and_9 (Col15[10], _0Set2, _0Set5, _0Set8);
  and and_10 (_0Set7, S7[1], ~S7[0]);  // AND_Gate
  and and_11 (_0Set6, S6[1], ~S6[0]);  // AND_Gate
  and and_12 (_789, _0Set7, _0Set8, _0Set9);
  and and_13 (Col25[10], _0Set3, _0Set6, _0Set9);
  and and_14 (_0Set9, S9[1], ~S9[0]);  // AND_Gate
  and and_15 (_0Set8, S8[1], ~S8[0]);  // AND_Gate
  and and_16 (Col0_plus[10], _0Set1, _0Set5, _0Set9);
  and and_17 (Col20_plus[0], _0Set3, _0Set5, _0Set7);
  or or_16 (Col4[6], Col0_plus[10], Col6[6]);
  or or_17 (Col4[5], _14[4], Col0_plus[5]);
  or or_18 (Col14[5], _24[4], Col0_plus[5]);
  or or_19 (Col24[5], _34[4], Col0_plus[5]);
  or or_20 (Col24[4], Col26[4], Col20_plus[0]);
  Pull_Resistor pull_resistor_1 (.node(M1));
  Pull_Resistor pull_resistor_2 (.node(M5));
  Pull_Resistor pull_resistor_3 (.node(M3));
  Pull_Resistor pull_resistor_4 (.node(M4));
  Pull_Resistor pull_resistor_5 (.node(M2));
  Pull_Resistor pull_resistor_6 (.node(M7));
  Pull_Resistor pull_resistor_7 (.node(M6));
  Pull_Resistor pull_resistor_8 (.node(M9));
  Pull_Resistor pull_resistor_9 (.node(M8));
  or or_21 (Col5[5], Col0_plus[10], or_24_out[4], Col0_plus[5]);
  or or_22 (Col15[5], Col15[10], or_25_out[4], Col0_plus[5]);
  or or_23 (Col25[5], Col20_plus[0], or_26_out[4], Col0_plus[5]);
  assign {Col5[1], Col5[2], Col5[3], Col5[4], or_24_out[4], Col5[6], Col5[7], Col5[8], Col5[9]} = {9{Col5[10]}} | _15;  // OR_Gate or_24, 9 bits wide
  assign {Col15[1], Col15[2], Col15[3], Col15[4], or_25_out[4], Col15[6], Col15[7], Col15[8], Col15[9]} = {9{Col15[10]}} | _25;  // OR_Gate or_25, 9 bits wide
  assign {Col25[1], Col25[2], Col25[3], Col25[4], or_26_out[4], Col25[6], Col25[7], Col25[8], Col25[9]} = {9{Col25[10]}} | _35;  // OR_Gate or_26, 9 bits wide
  or or_27 (Col6[5], _14[4], Col0_plus[5]);
  or or_28 (Col6[4], Col4[4], Col0_plus[10]);
  or or_29 (Col16[5], _24[4], Col0_plus[5]);
  or or_30 (Col26[6], Col20_plus[0], Col24[6]);
  or or_31 (Col26[5], _34[4], Col0_plus[5]);
  or or_32 (Col17[5], _23[4], Col0_plus[5]);
  or or_33 (Col27[7], Col20_plus[0], Col23[7]);
  or or_34 (Col27[5], _33[4], Col0_plus[5]);
  or or_35 (Col7[5], _13[4], Col0_plus[5]);
  or or_36 (Col7[3], Col3[3], Col0_plus[10]);
  or or_37 (Col8[5], _12[4], Col0_plus[5]);
  or or_38 (Col8[2], Col2[2], Col0_plus[10]);
  or or_39 (Col18[5], _22[4], Col0_plus[5]);
  or or_40 (Col28[8], Col20_plus[0], Col22[8]);
  or or_41 (Col28[5], _32[4], Col0_plus[5]);
  or or_42 (Col9[5], _11[4], Col0_plus[5]);
  or or_43 (Col9[1], Col1[1], Col0_plus[10]);
  or or_44 (Col19[5], _21[4], Col0_plus[5]);
  or or_45 (Col29[9], Col20_plus[0], Col21[9]);
  or or_46 (Col29[5], _31[4], Col0_plus[5]);

  assign Col0 = {12{1'b1}};
  assign {Col0_plus[11], Col0_plus[9:6], Col0_plus[4:0]} = 10'h200;
  assign {Col1[11:10], Col1[0]} = 3'b100;
  assign {Col2[11:10], Col2[0]} = 3'b100;
  assign {Col3[11:10], Col3[0]} = 3'b100;
  assign {Col4[11:10], Col4[0]} = 3'b100;
  assign {Col5[11], Col5[0]} = {1'b1, Col5[10]};
  assign {Col6[11:7], Col6[3:0]} = {2'b10, Col4[9:7], Col4[3:1], 1'b0};
  assign {Col7[11:8], Col7[6], Col7[4], Col7[2:0]} = {2'b10, Col3[9:8], Col3[6], Col3[4], Col3[2:1], 1'b0};
  assign {Col8[11:9], Col8[7:6], Col8[4:3], Col8[1:0]} = {2'b10, Col2[9], Col2[7:6], Col2[4:3], Col2[1], 1'b0};
  assign {Col9[11:10], Col9[8:6], Col9[4:2], Col9[0]} = {2'b10, Col1[8:6], Col1[4:2], 1'b0};
  assign Col10 = {12{1'b1}};
  assign Col10_minus = {6'b100000, Col0_plus[5], 4'b0000, Col0_plus[10]};
  assign Col10_plus = {6'b100000, Col0_plus[5], {5{1'b0}}};
  assign {Col11[11:10], Col11[0]} = 3'b100;
  assign {Col12[11:10], Col12[0]} = 3'b100;
  assign {Col13[11:10], Col13[0]} = 3'b100;
  assign {Col14[11:10], Col14[0]} = 3'b100;
  assign {Col15[11], Col15[0]} = {1'b1, Col15[10]};
  assign {Col16[11:6], Col16[4:0]} = {2'b10, Col14[9:6], Col14[4:1], 1'b0};
  assign {Col17[11:6], Col17[4:0]} = {2'b10, Col13[9:6], Col13[4:1], 1'b0};
  assign {Col18[11:6], Col18[4:0]} = {2'b10, Col12[9:6], Col12[4:1], 1'b0};
  assign {Col19[11:6], Col19[4:0]} = {2'b10, Col11[9:6], Col11[4:1], 1'b0};
  assign Col20 = {12{1'b1}};
  assign Col20_minus = {6'b100000, Col0_plus[5], {5{1'b0}}};
  assign Col20_plus[11:1] = {6'b100000, Col0_plus[5], 4'b0000};
  assign {Col21[11:10], Col21[0]} = 3'b100;
  assign {Col22[11:10], Col22[0]} = 3'b100;
  assign {Col23[11:10], Col23[0]} = 3'b100;
  assign {Col24[11:10], Col24[0]} = 3'b100;
  assign {Col25[11], Col25[0]} = {1'b1, Col25[10]};
  assign {Col26[11:7], Col26[3:0]} = {2'b10, Col24[9:7], Col24[3:1], 1'b0};
  assign {Col27[11:8], Col27[6], Col27[4], Col27[2:0]} = {2'b10, Col23[9:8], Col23[6], Col23[4], Col23[2:1], 1'b0};
  assign {Col28[11:9], Col28[7:6], Col28[4:3], Col28[1:0]} = {2'b10, Col22[9], Col22[7:6], Col22[4:3], Col22[1], 1'b0};
  assign {Col29[11:10], Col29[8:6], Col29[4:2], Col29[0]} = {2'b10, Col21[8:6], Col21[4:2], 1'b0};
  assign Col30 = {12{1'b1}};
  assign Col30_minus = {1'b1, Col20_plus[0], 4'b0000, Col0_plus[5], {5{1'b0}}};

  // Other names for the same wires on the sheet: _11 (some bits) = {Col1[1], Col1[2], Col1[3], Col1[4], Col1[6], Col1[7], Col1[8], Col9[9]};
  //   _12 (some bits) = {Col2[1], Col2[2], Col2[3], Col2[4], Col2[6], Col2[7], Col8[8], Col2[9]};
  //   _21 (some bits) = {Col11[1], Col11[2], Col11[3], Col11[4], Col11[6], Col11[7], Col11[8], Col11[9]};
  //   _22 (some bits) = {Col12[1], Col12[2], Col12[3], Col12[4], Col12[6], Col12[7], Col12[8], Col12[9]};
  //   _31 (some bits) = {Col29[1], Col21[2], Col21[3], Col21[4], Col21[6], Col21[7], Col21[8], Col21[9]};
  //   _32 (some bits) = {Col22[1], Col28[2], Col22[3], Col22[4], Col22[6], Col22[7], Col22[8], Col22[9]};
  //   _13 (some bits) = {Col3[1], Col3[2], Col3[3], Col3[4], Col3[6], Col7[7], Col3[8], Col3[9]};
  //   _14 (some bits) = {Col4[1], Col4[2], Col4[3], Col4[4], Col6[6], Col4[7], Col4[8], Col4[9]};
  //   _23 (some bits) = {Col13[1], Col13[2], Col13[3], Col13[4], Col13[6], Col13[7], Col13[8], Col13[9]};
  //   _24 (some bits) = {Col14[1], Col14[2], Col14[3], Col14[4], Col14[6], Col14[7], Col14[8], Col14[9]};
  //   _33 (some bits) = {Col23[1], Col23[2], Col27[3], Col23[4], Col23[6], Col23[7], Col23[8], Col23[9]};
  //   _34 (some bits) = {Col24[1], Col24[2], Col24[3], Col26[4], Col24[6], Col24[7], Col24[8], Col24[9]};
  //   _147 = Col5[10]; _258 = Col15[10]; _369 = Col25[10]; _159 = Col0_plus[10]; _123 = Col0_plus[5];
  //   _357 = Col20_plus[0]

  // Notes on the sheet:
  //   GATI
  //   2
  //   1
  //   3
  //   4
  //   5
  //   7
  //   6
  //   9
  //   8
endmodule

module Display_controller_bottom (
  input  [3:0] S3,
  input  [3:0] S7,
  input  [3:0] S2,
  input  [3:0] S4,
  input  [3:0] S6,
  input  [3:0] S8,
  input  [3:0] S1,
  input  [3:0] S5,
  input  [3:0] S9,
  output [24:0] Col0,
  output [24:0] Col0_plus,
  output [24:0] Col10_minus,
  output [24:0] Col1,
  output [24:0] Col2,
  output [24:0] Col3,
  output [24:0] Col4,
  output [24:0] Col5,
  output [24:0] Col6,
  output [24:0] Col7,
  output [24:0] Col8,
  output [24:0] Col9,
  output [24:0] Col10,
  output [24:0] Col10_plus,
  output [24:0] Col20_minus,
  output [24:0] Col16,
  output [24:0] Col11,
  output [24:0] Col12,
  output [24:0] Col13,
  output [24:0] Col14,
  output [24:0] Col15,
  output [24:0] Col17,
  output [24:0] Col18,
  output [24:0] Col19,
  output [24:0] Col20,
  output [24:0] Col20_plus,
  output [24:0] Col21,
  output [24:0] Col22,
  output [24:0] Col23,
  output [24:0] Col24,
  output [24:0] Col25,
  output [24:0] Col26,
  output [24:0] Col27,
  output [24:0] Col28,
  output [24:0] Col29,
  output [24:0] Col30_minus,
  output [24:0] Col30
);

  wire _0Set1, _0Set2, _0Set3, _0Set4, _0Set5, _0Set6, _0Set7, _0Set8, _0Set9, _123, M1, M2, M3, M4, M5, M6,
       M7, M8, M9;
  wire [4:4] _41, _42, _43, _44, _61, _62, _63, _64, _71, _72, _73, _74, _81, _82, _83, _84, _91, _92, _93,
       _94, or_39_out, or_40_out, or_44_out, or_45_out, or_67_out, or_70_out;
  wire [5:3] _54;
  wire [6:2] _53;
  wire [7:1] _52;
  wire [8:0] _11, _12, _13, _14, _15, _21, _22, _23, _24, _25, _31, _32, _33, _34, _35, _45, _51, _55, _65,
       _75, _85, _95;

  or or_1 (Col1[18], _41[4], Col0_plus[18]);
  or or_2 (Col1[6], _71[4], Col0_plus[6]);
  or or_3 (Col1[2], Col9[2], Col0_plus[1]);
  or or_4 (Col11[6], _81[4], Col0_plus[6]);
  or or_5 (Col21[18], _61[4], Col0_plus[18]);
  DisplayControl displaycontrol_1 (.\input (S1), .outSignals_1_2({_12, _11}), .outSignals_3_4_5({_15, _14, _13}));
  DisplayControl displaycontrol_2 (.\input (S2), .outSignals_1_2({_22, _21}), .outSignals_3_4_5({_25, _24, _23}));
  or or_6 (Col21[10], Col10_plus[23], Col29[10]);
  or or_7 (Col21[6], Col0_plus[6], _91[4]);
  DisplayControl displaycontrol_3 (
    .\input (S4),
    .outSignals_1_2({Col2[14], Col2[15], Col2[16], Col2[17], _42[4], Col2[19], Col2[20], Col2[21], Col2[22], Col1[14], Col1[15], Col1[16], Col1[17], _41[4], Col1[19], Col1[20], Col1[21], Col1[22]}),
    .outSignals_3_4_5({_45, Col4[14], Col4[15], Col4[16], Col4[17], _44[4], Col4[19], Col4[20], Col4[21], Col4[22], Col3[14], Col3[15], Col3[16], Col3[17], _43[4], Col3[19], Col3[20], Col3[21], Col3[22]}));
  DisplayControl displaycontrol_4 (.\input (S3), .outSignals_1_2({_32, _31}), .outSignals_3_4_5({_35, _34, _33}));
  DisplayControl displaycontrol_5 (
    .\input (S6),
    .outSignals_1_2({Col22[14], Col22[15], Col22[16], Col22[17], _62[4], Col22[19], Col22[20], Col22[21], Col22[22], Col21[14], Col21[15], Col21[16], Col21[17], _61[4], Col21[19], Col21[20], Col21[21], Col21[22]}),
    .outSignals_3_4_5({_65, Col24[14], Col24[15], Col24[16], Col24[17], _64[4], Col24[19], Col24[20], Col24[21], Col24[22], Col23[14], Col23[15], Col23[16], Col23[17], _63[4], Col23[19], Col23[20], Col23[21], Col23[22]}));
  DisplayControl displaycontrol_6 (
    .\input (S7),
    .outSignals_1_2({Col2[2], Col8[3], Col2[4], Col2[5], _72[4], Col2[7], Col2[8], Col2[9], Col2[10], Col9[2], Col1[3], Col1[4], Col1[5], _71[4], Col1[7], Col1[8], Col1[9], Col1[10]}),
    .outSignals_3_4_5({_75, Col4[2], Col4[3], Col4[4], Col6[5], _74[4], Col4[7], Col4[8], Col4[9], Col4[10], Col3[2], Col3[3], Col7[4], Col3[5], _73[4], Col3[7], Col3[8], Col3[9], Col3[10]}));
  DisplayControl displaycontrol_7 (
    .\input (S5),
    .outSignals_1_2({Col12[14], _52[7], Col12[16], Col12[17], _52[4], Col12[19], Col12[20], _52[1], Col12[22], _51[8], Col11[15], Col11[16], Col11[17], _51[4], Col11[19], Col11[20], Col11[21], _51[0]}),
    .outSignals_3_4_5({_55, Col14[14], Col14[15], Col14[16], _54, Col14[20], Col14[21], Col14[22], Col13[14], Col13[15], _53[6], Col13[17], _53[4], Col13[19], _53[2], Col13[21], Col13[22]}));
  or or_8 (Col2[18], _42[4], Col0_plus[18]);
  or or_9 (Col2[6], _72[4], Col0_plus[6]);
  or or_10 (Col2[3], Col8[3], Col0_plus[1]);
  or or_11 (Col11[22], Col10_plus[23], _51[0]);
  or or_12 (Col11[18], _51[4], Col0_plus[18]);
  or or_13 (Col11[14], _51[8], Col0_plus[1]);
  DisplayControl displaycontrol_8 (
    .\input (S9),
    .outSignals_1_2({Col22[2], Col22[3], Col22[4], Col22[5], _92[4], Col22[7], Col22[8], Col28[9], Col22[10], Col21[2], Col21[3], Col21[4], Col21[5], _91[4], Col21[7], Col21[8], Col21[9], Col29[10]}),
    .outSignals_3_4_5({_95, Col24[2], Col24[3], Col24[4], Col24[5], _94[4], Col26[7], Col24[8], Col24[9], Col24[10], Col23[2], Col23[3], Col23[4], Col23[5], _93[4], Col23[7], Col27[8], Col23[9], Col23[10]}));
  DisplayControl displaycontrol_9 (
    .\input (S8),
    .outSignals_1_2({Col12[2], Col12[3], Col12[4], Col12[5], _82[4], Col12[7], Col12[8], Col12[9], Col12[10], Col11[2], Col11[3], Col11[4], Col11[5], _81[4], Col11[7], Col11[8], Col11[9], Col11[10]}),
    .outSignals_3_4_5({_85, Col14[2], Col14[3], Col14[4], Col14[5], _84[4], Col14[7], Col14[8], Col14[9], Col14[10], Col13[2], Col13[3], Col13[4], Col13[5], _83[4], Col13[7], Col13[8], Col13[9], Col13[10]}));
  or or_14 (Col22[18], _62[4], Col0_plus[18]);
  or or_15 (Col22[6], Col0_plus[6], _92[4]);
  or or_16 (Col22[9], Col10_plus[23], Col28[9]);
  or or_17 (Col3[18], _43[4], Col0_plus[18]);
  or or_18 (Col3[6], _73[4], Col0_plus[6]);
  or or_19 (Col3[4], Col7[4], Col0_plus[1]);
  or or_20 (Col12[6], _82[4], Col0_plus[6]);
  and and_1 (_0Set2, S2[1], ~S2[0]);  // AND_Gate
  and and_2 (_0Set1, S1[1], ~S1[0]);  // AND_Gate
  and and_3 (_123, _0Set1, _0Set2, _0Set3);
  and and_4 (Col5[23], _0Set1, _0Set4, _0Set7);
  or or_21 (Col23[18], _63[4], Col0_plus[18]);
  and and_5 (_0Set4, S4[1], ~S4[0]);  // AND_Gate
  and and_6 (_0Set5, S5[1], ~S5[0]);  // AND_Gate
  and and_7 (_0Set3, S3[1], ~S3[0]);  // AND_Gate
  and and_8 (Col0_plus[18], _0Set4, _0Set5, _0Set6);
  and and_9 (Col15[23], _0Set2, _0Set5, _0Set8);
  or or_22 (Col12[21], Col10_plus[23], _52[1]);
  or or_23 (Col12[18], _52[4], Col0_plus[18]);
  or or_24 (Col12[15], _52[7], Col0_plus[1]);
  or or_25 (Col23[8], Col10_plus[23], Col27[8]);
  or or_26 (Col23[6], Col0_plus[6], _93[4]);
  and and_10 (_0Set7, S7[1], ~S7[0]);  // AND_Gate
  and and_11 (_0Set6, S6[1], ~S6[0]);  // AND_Gate
  and and_12 (Col0_plus[6], _0Set7, _0Set8, _0Set9);
  and and_13 (Col25[23], _0Set3, _0Set6, _0Set9);
  or or_27 (Col4[18], _44[4], Col0_plus[18]);
  or or_28 (Col4[6], _74[4], Col0_plus[6]);
  or or_29 (Col4[5], Col6[5], Col0_plus[1]);
  and and_14 (_0Set9, S9[1], ~S9[0]);  // AND_Gate
  and and_15 (_0Set8, S8[1], ~S8[0]);  // AND_Gate
  and and_16 (Col10_plus[23], _0Set1, _0Set5, _0Set9);
  and and_17 (Col0_plus[1], _0Set3, _0Set5, _0Set7);
  or or_30 (Col24[18], _64[4], Col0_plus[18]);
  Pull_Resistor pull_resistor_1 (.node(M1));
  or or_31 (Col13[6], _83[4], Col0_plus[6]);
  or or_32 (Col24[7], Col10_plus[23], Col26[7]);
  or or_33 (Col24[6], Col0_plus[6], _94[4]);
  Pull_Resistor pull_resistor_2 (.node(M2));
  Pull_Resistor pull_resistor_3 (.node(M3));
  Pull_Resistor pull_resistor_4 (.node(M5));
  Pull_Resistor pull_resistor_5 (.node(M4));
  or or_34 (Col5[18], or_39_out[4], Col0_plus[18]);
  or or_35 (Col5[6], Col0_plus[1], or_40_out[4], Col0_plus[6]);
  Pull_Resistor pull_resistor_6 (.node(M6));
  Pull_Resistor pull_resistor_7 (.node(M9));
  Pull_Resistor pull_resistor_8 (.node(M8));
  Pull_Resistor pull_resistor_9 (.node(M7));
  or or_36 (Col13[20], Col10_plus[23], _53[2]);
  or or_37 (Col13[18], _53[4], Col0_plus[18]);
  or or_38 (Col13[16], _53[6], Col0_plus[1]);
  assign {Col5[14], Col5[15], Col5[16], Col5[17], or_39_out[4], Col5[19], Col5[20], Col5[21], Col5[22]} = {9{Col5[23]}} | _45;  // OR_Gate or_39, 9 bits wide
  assign {Col5[2], Col5[3], Col5[4], Col5[5], or_40_out[4], Col5[7], Col5[8], Col5[9], Col5[10]} = {9{Col5[23]}} | _75;  // OR_Gate or_40, 9 bits wide
  or or_41 (Col25[18], or_44_out[4], Col0_plus[18]);
  or or_42 (Col25[6], Col10_plus[23], or_45_out[4], Col0_plus[6]);
  or or_43 (Col14[6], _84[4], Col0_plus[6]);
  assign {Col25[14], Col25[15], Col25[16], Col25[17], or_44_out[4], Col25[19], Col25[20], Col25[21], Col25[22]} = {9{Col25[23]}} | _65;  // OR_Gate or_44, 9 bits wide
  assign {Col25[2], Col25[3], Col25[4], Col25[5], or_45_out[4], Col25[7], Col25[8], Col25[9], Col25[10]} = {9{Col25[23]}} | _95;  // OR_Gate or_45, 9 bits wide
  or or_46 (Col6[18], _44[4], Col0_plus[18]);
  or or_47 (Col6[7], Col0_plus[1], Col4[7]);
  or or_48 (Col6[6], Col0_plus[6], _74[4]);
  or or_49 (Col26[18], _64[4], Col0_plus[18]);
  or or_50 (Col26[6], _94[4], Col0_plus[6]);
  or or_51 (Col26[5], Col24[5], Col10_plus[23]);
  or or_52 (Col14[19], Col10_plus[23], _54[3]);
  or or_53 (Col14[18], _54[4], Col0_plus[18]);
  or or_54 (Col14[17], _54[5], Col0_plus[1]);
  or or_55 (Col7[18], _43[4], Col0_plus[18]);
  or or_56 (Col7[8], Col0_plus[1], Col3[8]);
  or or_57 (Col7[6], Col0_plus[6], _73[4]);
  or or_58 (Col15[6], or_67_out[4], Col0_plus[6]);
  or or_59 (Col27[18], _63[4], Col0_plus[18]);
  or or_60 (Col27[6], _93[4], Col0_plus[6]);
  or or_61 (Col27[4], Col23[4], Col10_plus[23]);
  or or_62 (Col8[18], _42[4], Col0_plus[18]);
  or or_63 (Col8[6], Col0_plus[6], _72[4]);
  or or_64 (Col15[18], Col10_plus[23], Col0_plus[1], or_70_out[4], Col0_plus[18]);
  or or_65 (Col28[18], _62[4], Col0_plus[18]);
  or or_66 (Col8[9], Col0_plus[1], Col2[9]);
  assign {Col15[2], Col15[3], Col15[4], Col15[5], or_67_out[4], Col15[7], Col15[8], Col15[9], Col15[10]} = {9{Col15[23]}} | _85;  // OR_Gate or_67, 9 bits wide
  or or_68 (Col28[6], _92[4], Col0_plus[6]);
  or or_69 (Col28[3], Col22[3], Col10_plus[23]);
  assign {Col15[14], Col15[15], Col15[16], Col15[17], or_70_out[4], Col15[19], Col15[20], Col15[21], Col15[22]} = {9{Col15[23]}} | _55;  // OR_Gate or_70, 9 bits wide
  or or_71 (Col9[18], _41[4], Col0_plus[18]);
  or or_72 (Col29[18], _61[4], Col0_plus[18]);
  or or_73 (Col29[2], Col21[2], Col10_plus[23]);
  or or_74 (Col9[10], Col0_plus[1], Col1[10]);
  or or_75 (Col9[6], Col0_plus[6], _71[4]);
  or or_76 (Col16[6], _84[4], Col0_plus[6]);
  or or_77 (Col29[6], _91[4], Col0_plus[6]);
  or or_78 (Col16[19], Col0_plus[1], _54[3]);
  or or_79 (Col16[18], _54[4], Col0_plus[18]);
  or or_80 (Col16[17], _54[5], Col10_plus[23]);
  or or_81 (Col17[6], _83[4], Col0_plus[6]);
  or or_82 (Col17[20], Col0_plus[1], _53[2]);
  or or_83 (Col17[18], _53[4], Col0_plus[18]);
  or or_84 (Col17[16], _53[6], Col10_plus[23]);
  or or_85 (Col18[6], _82[4], Col0_plus[6]);
  or or_86 (Col18[21], Col0_plus[1], _52[1]);
  or or_87 (Col18[18], _52[4], Col0_plus[18]);
  or or_88 (Col18[15], _52[7], Col10_plus[23]);
  or or_89 (Col19[6], _81[4], Col0_plus[6]);
  or or_90 (Col19[22], Col0_plus[1], _51[0]);
  or or_91 (Col19[18], _51[4], Col0_plus[18]);
  or or_92 (Col19[14], _51[8], Col10_plus[23]);

  assign Col0 = {25{1'b1}};
  assign {Col0_plus[24:19], Col0_plus[17:7], Col0_plus[5:2], Col0_plus[0]} = 22'h200401;
  assign {Col1[24:23], Col1[13:11], Col1[1:0]} = 7'b1001001;
  assign {Col2[24:23], Col2[13:11], Col2[1:0]} = 7'b1001001;
  assign {Col3[24:23], Col3[13:11], Col3[1:0]} = 7'b1001001;
  assign {Col4[24:23], Col4[13:11], Col4[1:0]} = 7'b1001001;
  assign {Col5[24], Col5[13:11], Col5[1:0]} = {1'b1, Col5[23], 1'b1, {2{Col5[23]}}, 1'b1};
  assign {Col6[24:19], Col6[17:8], Col6[4:0]} = {2'b10, Col4[22:19], Col4[17:14], 3'b010, Col4[10:8], Col4[4:2], 2'b01};
  assign {Col7[24:19], Col7[17:9], Col7[7], Col7[5], Col7[3:0]} = {2'b10, Col3[22:19], Col3[17:14], 3'b010, Col3[10:9], Col3[7], Col3[5], Col3[3:2], 2'b01};
  assign {Col8[24:19], Col8[17:10], Col8[8:7], Col8[5:4], Col8[2:0]} = {2'b10, Col2[22:19], Col2[17:14], 3'b010, Col2[10], Col2[8:7], Col2[5:4], Col2[2], 2'b01};
  assign {Col9[24:19], Col9[17:11], Col9[9:7], Col9[5:3], Col9[1:0]} = {2'b10, Col1[22:19], Col1[17:14], 3'b010, Col1[9:7], Col1[5:3], 2'b01};
  assign Col10 = {25{1'b1}};
  assign Col10_minus = {6'b100000, Col0_plus[18], 6'b000001, Col0_plus[1], 4'b0000, Col0_plus[6], 6'b000001};
  assign {Col10_plus[24], Col10_plus[22:0]} = {5'b10000, Col0_plus[18], 4'b0000, Col0_plus[1], 6'b100000, Col0_plus[6], 6'b000001};
  assign {Col11[24:23], Col11[13:11], Col11[1:0]} = 7'b1001001;
  assign {Col12[24:23], Col12[13:11], Col12[1:0]} = 7'b1001001;
  assign {Col13[24:23], Col13[13:11], Col13[1:0]} = 7'b1001001;
  assign {Col14[24:23], Col14[13:11], Col14[1:0]} = 7'b1001001;
  assign {Col15[24], Col15[13:11], Col15[1:0]} = {1'b1, Col15[23], 1'b1, {2{Col15[23]}}, 1'b1};
  assign {Col16[24:20], Col16[16:7], Col16[5:0]} = {2'b10, Col14[22:20], Col14[16:14], 3'b010, Col14[10:7], Col14[5:2], 2'b01};
  assign {Col17[24:21], Col17[19], Col17[17], Col17[15:7], Col17[5:0]} = {2'b10, Col13[22:21], Col13[19], Col13[17], Col13[15:14], 3'b010, Col13[10:7], Col13[5:2], 2'b01};
  assign {Col18[24:22], Col18[20:19], Col18[17:16], Col18[14:7], Col18[5:0]} = {2'b10, Col12[22], Col12[20:19], Col12[17:16], Col12[14], 3'b010, Col12[10:7], Col12[5:2], 2'b01};
  assign {Col19[24:23], Col19[21:19], Col19[17:15], Col19[13:7], Col19[5:0]} = {2'b10, Col11[21:19], Col11[17:15], 3'b010, Col11[10:7], Col11[5:2], 2'b01};
  assign Col20 = {25{1'b1}};
  assign Col20_minus = {1'b1, Col0_plus[1], 4'b0000, Col0_plus[18], 4'b0000, Col10_plus[23], 6'b100000, Col0_plus[6], 6'b000001};
  assign Col20_plus = {6'b100000, Col0_plus[18], 6'b000001, Col10_plus[23], 4'b0000, Col0_plus[6], 6'b000001};
  assign {Col21[24:23], Col21[13:11], Col21[1:0]} = 7'b1001001;
  assign {Col22[24:23], Col22[13:11], Col22[1:0]} = 7'b1001001;
  assign {Col23[24:23], Col23[13:11], Col23[1:0]} = 7'b1001001;
  assign {Col24[24:23], Col24[13:11], Col24[1:0]} = 7'b1001001;
  assign {Col25[24], Col25[13:11], Col25[1:0]} = {1'b1, Col25[23], 1'b1, {2{Col25[23]}}, 1'b1};
  assign {Col26[24:19], Col26[17:8], Col26[4:0]} = {2'b10, Col24[22:19], Col24[17:14], 3'b010, Col24[10:8], Col24[4:2], 2'b01};
  assign {Col27[24:19], Col27[17:9], Col27[7], Col27[5], Col27[3:0]} = {2'b10, Col23[22:19], Col23[17:14], 3'b010, Col23[10:9], Col23[7], Col23[5], Col23[3:2], 2'b01};
  assign {Col28[24:19], Col28[17:10], Col28[8:7], Col28[5:4], Col28[2:0]} = {2'b10, Col22[22:19], Col22[17:14], 3'b010, Col22[10], Col22[8:7], Col22[5:4], Col22[2], 2'b01};
  assign {Col29[24:19], Col29[17:11], Col29[9:7], Col29[5:3], Col29[1:0]} = {2'b10, Col21[22:19], Col21[17:14], 3'b010, Col21[9:7], Col21[5:3], 2'b01};
  assign Col30 = {25{1'b1}};
  assign Col30_minus = {6'b100000, Col0_plus[18], 11'h20, Col0_plus[6], 4'b0000, Col10_plus[23], 1'b1};

  // Other names for the same wires on the sheet: _43 (some bits) = {Col3[14], Col3[15], Col3[16], Col3[17], Col3[19], Col3[20], Col3[21], Col3[22]};
  //   _44 (some bits) = {Col4[14], Col4[15], Col4[16], Col4[17], Col4[19], Col4[20], Col4[21], Col4[22]};
  //   _41 (some bits) = {Col1[14], Col1[15], Col1[16], Col1[17], Col1[19], Col1[20], Col1[21], Col1[22]};
  //   _42 (some bits) = {Col2[14], Col2[15], Col2[16], Col2[17], Col2[19], Col2[20], Col2[21], Col2[22]};
  //   _51 (some bits) = {Col11[15], Col11[16], Col11[17], Col11[19], Col11[20], Col11[21]};
  //   _52 (some bits) = {Col12[14], Col12[16], Col12[17], Col12[19], Col12[20], Col12[22]};
  //   _53 (some bits) = {Col13[14], Col13[15], Col13[17], Col13[19], Col13[21], Col13[22]};
  //   _54 (some bits) = {Col14[14], Col14[15], Col14[16], Col14[20], Col14[21], Col14[22]};
  //   _63 (some bits) = {Col23[14], Col23[15], Col23[16], Col23[17], Col23[19], Col23[20], Col23[21], Col23[22]};
  //   _64 (some bits) = {Col24[14], Col24[15], Col24[16], Col24[17], Col24[19], Col24[20], Col24[21], Col24[22]};
  //   _71 (some bits) = {Col9[2], Col1[3], Col1[4], Col1[5], Col1[7], Col1[8], Col1[9], Col1[10]};
  //   _72 (some bits) = {Col2[2], Col8[3], Col2[4], Col2[5], Col2[7], Col2[8], Col2[9], Col2[10]};
  //   _73 (some bits) = {Col3[2], Col3[3], Col7[4], Col3[5], Col3[7], Col3[8], Col3[9], Col3[10]};
  //   _74 (some bits) = {Col4[2], Col4[3], Col4[4], Col6[5], Col4[7], Col4[8], Col4[9], Col4[10]};
  //   _81 (some bits) = {Col11[2], Col11[3], Col11[4], Col11[5], Col11[7], Col11[8], Col11[9], Col11[10]};
  //   _82 (some bits) = {Col12[2], Col12[3], Col12[4], Col12[5], Col12[7], Col12[8], Col12[9], Col12[10]};
  //   _83 (some bits) = {Col13[2], Col13[3], Col13[4], Col13[5], Col13[7], Col13[8], Col13[9], Col13[10]};
  //   _84 (some bits) = {Col14[2], Col14[3], Col14[4], Col14[5], Col14[7], Col14[8], Col14[9], Col14[10]};
  //   _91 (some bits) = {Col21[2], Col21[3], Col21[4], Col21[5], Col21[7], Col21[8], Col21[9], Col29[10]};
  //   _92 (some bits) = {Col22[2], Col22[3], Col22[4], Col22[5], Col22[7], Col22[8], Col28[9], Col22[10]};
  //   _93 (some bits) = {Col23[2], Col23[3], Col23[4], Col23[5], Col23[7], Col27[8], Col23[9], Col23[10]};
  //   _94 (some bits) = {Col24[2], Col24[3], Col24[4], Col24[5], Col26[7], Col24[8], Col24[9], Col24[10]};
  //   _61 (some bits) = {Col21[14], Col21[15], Col21[16], Col21[17], Col21[19], Col21[20], Col21[21], Col21[22]};
  //   _62 (some bits) = {Col22[14], Col22[15], Col22[16], Col22[17], Col22[19], Col22[20], Col22[21], Col22[22]};
  //   _147 = Col5[23]; _369 = Col25[23]; _258 = Col15[23]; _789 = Col0_plus[6]; _159 = Col10_plus[23];
  //   _456 = Col0_plus[18]; _357 = Col0_plus[1]

  // Notes on the sheet:
  //   GATI
  //   2
  //   1
  //   3
  //   4
  //   5
  //   7
  //   6
  //   9
  //   8
endmodule

module Win_loose_Detector (
  input  [3:0] S1,
  input  [3:0] S2,
  input  [3:0] S3,
  input  [3:0] S4,
  input  [3:0] S5,
  input  [3:0] S6,
  input  [3:0] S7,
  input  [3:0] S8,
  input  [3:0] S9,
  output [7:0] Winner
);

  wire and_3_out, and_4_out, and_7_out, and_8_out, and_13_out, and_14_out, and_17_out, and_18_out,
       and_21_out, and_22_out, and_25_out, and_26_out, and_29_out, and_30_out, and_33_out, and_34_out,
       not_8_out, or_1_out, or_2_out, or_3_out, S1_0, S1_X, S1_Z, S2_0, S2_X, S2_Z, S3_0, S3_X, S3_Z, S4_0,
       S4_X, S4_Z, S5_0, S5_X, S5_Z, S6_0, S6_X, S6_Z, S7_0, S7_X, S7_Z, S8_0, S8_X, S8_Z, S9_0, S9_X, S9_Z;
  wire [7:0] controlled_buffer_1_out;

  and and_1 (S1_0, S1[1], ~S1[0]);  // AND_Gate
  and and_2 (S1_X, S1[1], S1[0]);
  not not_1 (S1_Z, S1[1]);
  and and_3 (and_3_out, S1_0, S2_0, S3_0);
  and and_4 (and_4_out, S1_X, S2_X, S3_X);
  and and_5 (S2_X, S2[1], S2[0]);
  and and_6 (S2_0, S2[1], ~S2[0]);  // AND_Gate
  not not_2 (S2_Z, S2[1]);
  and and_7 (and_7_out, S4_0, S5_0, S6_0);
  and and_8 (and_8_out, S4_X, S5_X, S6_X);
  and and_9 (S3_0, S3[1], ~S3[0]);  // AND_Gate
  and and_10 (S3_X, S3[1], S3[0]);
  not not_3 (S3_Z, S3[1]);
  and and_11 (S4_X, S4[1], S4[0]);
  and and_12 (S4_0, S4[1], ~S4[0]);  // AND_Gate
  not not_4 (S4_Z, S4[1]);
  and and_13 (and_13_out, S7_0, S8_0, S9_0);
  and and_14 (and_14_out, S7_X, S8_X, S9_X);
  and and_15 (S5_X, S5[1], S5[0]);
  and and_16 (S5_0, S5[1], ~S5[0]);  // AND_Gate
  not not_5 (S5_Z, S5[1]);
  and and_17 (and_17_out, S1_0, S4_0, S7_0);
  or or_1 (or_1_out, and_3_out, and_7_out, and_13_out, and_17_out, and_21_out, and_25_out, and_29_out, and_33_out);
  assign controlled_buffer_1_out = or_1_out ? 8'h2 : 8'bz;  // Controlled_Buffer controlled_buffer_1
  assign controlled_buffer_1_out = or_2_out ? 8'h3 : 8'bz;  // Controlled_Buffer controlled_buffer_2
  or or_2 (or_2_out, and_4_out, and_8_out, and_14_out, and_18_out, and_22_out, and_26_out, and_30_out, and_34_out);
  and and_18 (and_18_out, S1_X, S4_X, S7_X);
  and and_19 (S6_X, S6[1], S6[0]);
  and and_20 (S6_0, S6[1], ~S6[0]);  // AND_Gate
  not not_6 (S6_Z, S6[1]);
  and and_21 (and_21_out, S2_0, S5_0, S8_0);
  and and_22 (and_22_out, S2_X, S5_X, S8_X);
  and and_23 (S7_X, S7[1], S7[0]);
  and and_24 (S7_0, S7[1], ~S7[0]);  // AND_Gate
  not not_7 (S7_Z, S7[1]);
  and and_25 (and_25_out, S3_0, S6_0, S9_0);
  or or_3 (or_3_out, S1_Z, S2_Z, S3_Z, S4_Z, S5_Z, S6_Z, S7_Z, S8_Z, S9_Z);
  not not_8 (not_8_out, or_3_out);
  assign Winner = not_8_out ? 8'h1 : 8'bz;  // Controlled_Buffer controlled_buffer_3
  assign Winner = or_3_out ? controlled_buffer_1_out : 8'bz;  // Controlled_Buffer controlled_buffer_4
  and and_26 (and_26_out, S3_X, S6_X, S9_X);
  and and_27 (S8_0, S8[1], ~S8[0]);  // AND_Gate
  and and_28 (S8_X, S8[1], S8[0]);
  not not_9 (S8_Z, S8[1]);
  and and_29 (and_29_out, S1_0, S5_0, S9_0);
  Pull_Resistor pull_resistor_1 (.node(Winner));
  and and_30 (and_30_out, S1_X, S5_X, S9_X);
  and and_31 (S9_X, S9[1], S9[0]);
  and and_32 (S9_0, S9[1], ~S9[0]);  // AND_Gate
  not not_10 (S9_Z, S9[1]);
  and and_33 (and_33_out, S3_0, S5_0, S7_0);
  and and_34 (and_34_out, S3_X, S5_X, S7_X);

  // Notes on the sheet:
  //   000
  //   ---
  //   ---
  //   XXX
  //   ---
  //   ---
  //   ---
  //   000
  //   ---
  //   ---
  //   XXX
  //   ---
  //   ---
  //   XXX
  //   ---
  //   ---
  //   000
  //   ---
  //   0--
  //   0--
  //   0--
  //   X--
  //   X--
  //   X--
  //   -0-
  //   -0-
  //   -0-
  //   -X-
  //   -X-
  //   -X-
  //   --0
  //   --0
  //   --0
  //   --X
  //   --X
  //   --X
  //   0--
  //   -0-
  //   --0
  //   X--
  //   -X-
  //   --X
  //   --0
  //   -0-
  //   0--
  //   --X
  //   -X-
  //   X--
endmodule
